# Fritzing sketch blynk_GPIO (saved by Fritzing 0.9.3b)
breadboards: 1

parts:
  Raspberry_Pi_1 = Raspberry Pi 3 [part_number=RPI-3-V1.2]
  S1 = Pushbutton [package="[THT]"]
  R1 = Resistor [tolerance=±5% resistance=220 package=THT]
  R2 = Resistor [tolerance=±5% resistance=1k package=THT]
  R3 = Resistor [tolerance=±5% resistance=220 package=THT]
  LED1 = LED - 5mm [color="Green (555nm)" package="5 mm [THT]"]
  LED2 = LED - 5mm [color="Red (633nm)" package="5 mm [THT]"]

nets:
  3V3: Raspberry_Pi_1.3v3, Raspberry_Pi_1.3V3, S1.Pin_3, S1.Pin_4
  N1: Raspberry_Pi_1.GPIO21, LED2.anode
  N2: Raspberry_Pi_1.GPIO20, LED1.anode
  N3: Raspberry_Pi_1.GPIO16, S1.Pin_1, S1.Pin_2, R2.Pin_1
  N4: Raspberry_Pi_1.GND, R1.Pin_1, R2.Pin_0, R3.Pin_1
  N5: R1.Pin_0, LED2.cathode
  N6: R3.Pin_0, LED1.cathode
